// Logisim project CAN_receiver.circ as structural Verilog: 1 circuit, main circuit main
module main (
  input  in_1
);

  wire and_1_out, and_2_out, and_3_out, and_4_out, clock_1_out, d_ff_1_q, d_ff_2_q, d_ff_3_q, not_1_out,
       not_2_out, not_3_out, t_ff_1_q, t_ff_1_qn, t_ff_2_qn, t_ff_3_qn, t_ff_4_q;

  Clock clock_1 (.out(clock_1_out));
  D_Flip_Flop d_ff_1 (.D(not_1_out), .clk(clock_1_out), .Q(d_ff_1_q));  // open: Qn, preset, reset
  not not_1 (not_1_out, in_1);
  and and_1 (and_1_out, in_1, and_3_out);
  not not_2 (not_2_out, and_3_out);
  D_Flip_Flop d_ff_2 (.D(and_1_out), .clk(clock_1_out), .Q(d_ff_2_q));  // open: Qn, preset, reset
  and and_2 (and_2_out, d_ff_1_q, not_2_out);
  D_Flip_Flop d_ff_3 (.D(d_ff_2_q), .clk(clock_1_out), .Q(d_ff_3_q));  // open: Qn, preset, reset
  T_Flip_Flop t_ff_1 (.T(and_2_out), .clk(clock_1_out), .Q(t_ff_1_q), .Qn(t_ff_1_qn));  // open: reset, preset
  and and_3 (and_3_out, t_ff_4_q, t_ff_1_q);
  not not_3 (not_3_out, d_ff_2_q);
  T_Flip_Flop t_ff_2 (.T(and_2_out), .clk(t_ff_1_qn), .Qn(t_ff_2_qn));  // open: Q, reset, preset
  and and_4 (and_4_out, not_3_out, d_ff_3_q);
  T_Flip_Flop t_ff_3 (.T(and_2_out), .clk(t_ff_2_qn), .Qn(t_ff_3_qn));  // open: Q, reset, preset
  T_Flip_Flop t_ff_4 (.T(and_2_out), .clk(t_ff_3_qn), .Q(t_ff_4_q));  // open: Qn, reset, preset
endmodule
