// Logisim project iter1.circ as structural Verilog: 1 circuit, main circuit main
module main (
  input  [7:0] in_1
);

  wire clock_1_out, d_ff_1_q, d_ff_1_qn, d_ff_2_q, d_ff_2_qn, d_ff_3_q, d_ff_3_qn, shift_register_1_p12;
  wire [7:0] counter_1_q, rom_1_data;

  D_Flip_Flop d_ff_1 (.D(d_ff_1_qn), .clk(clock_1_out), .Q(d_ff_1_q), .Qn(d_ff_1_qn));  // open: preset, reset
  Clock clock_1 (.out(clock_1_out));
  D_Flip_Flop d_ff_2 (.D(d_ff_2_qn), .clk(d_ff_1_q), .Q(d_ff_2_q), .Qn(d_ff_2_qn));  // open: preset, reset
  D_Flip_Flop d_ff_3 (.D(d_ff_3_qn), .clk(d_ff_2_q), .Q(d_ff_3_q), .Qn(d_ff_3_qn));  // open: preset, reset
  Counter counter_1 (
    .load(1'b1), .up(1'b0), .count(1'b1), .clk(d_ff_3_q), .D(in_1), .Q(counter_1_q));  // open: clr, carry
  ROM rom_1 (.addr(counter_1_q), .data(rom_1_data));
  // Shift_Register #(.length(7)) shift_register_1: pin names not known; wires that end beside it: 1'b1, 1'b1, clock_1_out, rom_1_data[0], rom_1_data[1], rom_1_data[2], rom_1_data[3], rom_1_data[4], rom_1_data[5], rom_1_data[6], rom_1_data[7], shift_register_1_p12
  // Probe on shift_register_1_p12

  // Notes on the sheet:
  //   in_1: initial=0x101
  //   contents of rom_1 (hex, n*v repeats v):
  //   11 1
endmodule
